# Fritzing sketch esp32cam_nodered_mitPIR (saved by Fritzing 0.9.10b)
breadboards: 1

parts:
  Mod1 = ESP32 - CAM
  JACK1 = 2.1mm Barrel Jack with Terminal Block
  Bauteil1 = FTDI Basic Programmer
  Q1 = NPN-Transistor [part_number=BC549 package="TO92 [THT]"]
  R1 = Resistor [tolerance=±5% resistance=1k package="0603 [SMD]"]
  PIR2 = PIR sensor
  R2 = Resistor [tolerance=±5% resistance=10k package="0603 [SMD]"]

nets:
  5V: Mod1.5V, JACK1.POS, Bauteil1.POWER, PIR2.VDD
  N1: Mod1.IO13, R2.Pin_0
  GND: Mod1.GND, JACK1.NEG, Bauteil1.RXI, Bauteil1.TXO, Bauteil1.GND, Q1.E, PIR2.GND
  N2: Q1.B, R2.Pin_1
  N3: Q1.C, R1.Pin_0
  N4: R1.Pin_1, PIR2.SIG

notes:
  10k
  1k
  NPN
  BC549
  FTDI VCC Verbindung nur während Flash-Vorgang

custom parts:
  ESP32 - CAM: The ESP32-CAM has a very competitive small-size camera module that can operate independently as a minimum system with a footprint of only 27*40.5*4.5mm and a deep sleep current of up to 6mA.
