# Fritzing sketch wiring (saved by Fritzing 0.9.10b)
breadboards: 1

parts:
  MH-ET_Live_Minikit_for_ESP1 = MH-ET Live Minikit for ESP32
  LED1 = smd LED [color="Red (633nm)" package="0603 [SMD]"]
  LED2 = smd LED [color="Green (555nm)" package="0603 [SMD]"]
  Bauteil1 = RFID-RC522-v2
  R1 = Resistor [tolerance=±5% resistance=220 package="2512 [SMD]"]
  R2 = Resistor [tolerance=±5% resistance=220 package="2512 [SMD]"]

nets:
  GND: MH-ET_Live_Minikit_for_ESP1.GND, LED1.cathode, LED2.cathode, Bauteil1.GND
  N1: MH-ET_Live_Minikit_for_ESP1.IO26, Bauteil1.SDA
  N2: MH-ET_Live_Minikit_for_ESP1.IO18, Bauteil1.SCK
  N3: MH-ET_Live_Minikit_for_ESP1.IO19, Bauteil1.MISO
  N4: MH-ET_Live_Minikit_for_ESP1.IO23, Bauteil1.MOSI
  N5: MH-ET_Live_Minikit_for_ESP1.IO5, Bauteil1.RST
  3.3V: MH-ET_Live_Minikit_for_ESP1.3.3V, Bauteil1.3.3V
  N6: MH-ET_Live_Minikit_for_ESP1.IO22, R1.Pin_0
  N7: MH-ET_Live_Minikit_for_ESP1.IO21, R2.Pin_0
  N8: LED1.anode, R2.Pin_1
  N9: LED2.anode, R1.Pin_1

notes:
  SDA SCK MOSI MISO IRQ GND RST 3,3V

custom parts:
  MH-ET Live Minikit for ESP32: MH-ET Live Minikit for ESP32 ( http://mh.nodebb.com/topic/8/mh-et-live-minikit-for-esp32/2/) PCB footprint is invalid.
  RFID-RC522-v2: A simple China made RFID-RC522 Reader; do check the pin labels, as this is a MFRC522 based clone.
