# Fritzing sketch miniwetterstation (saved by Fritzing 0.9.10b)
breadboards: 1

parts:
  MH-ET_Live_Minikit_for_ESP1 = MH-ET Live Minikit for ESP32
  Bauteil2 = BH1750
  Bauteil3 = Adafruit BMP180
  F1 = Small Fan, based on Fan - Ventilador [package=THT]

nets:
  GND: MH-ET_Live_Minikit_for_ESP1.GND, Bauteil2.GND, Bauteil3.GND, F1.GND
  N1: MH-ET_Live_Minikit_for_ESP1.SVP, MH-ET_Live_Minikit_for_ESP1.IO26, MH-ET_Live_Minikit_for_ESP1.IO18, MH-ET_Live_Minikit_for_ESP1.IO19, MH-ET_Live_Minikit_for_ESP1.IO23, F1.5V
  N2: MH-ET_Live_Minikit_for_ESP1.TCK, MH-ET_Live_Minikit_for_ESP1.SD3
  N3: MH-ET_Live_Minikit_for_ESP1.RXD, MH-ET_Live_Minikit_for_ESP1.IO22, MH-ET_Live_Minikit_for_ESP1.IO21, MH-ET_Live_Minikit_for_ESP1.IO17, MH-ET_Live_Minikit_for_ESP1.IO16, Bauteil2.SCL, Bauteil2.SDA, Bauteil3.SCL, Bauteil3.SDA
  VCC: MH-ET_Live_Minikit_for_ESP1.VCC, Bauteil2.VCC, Bauteil3.+5V
  N4: MH-ET_Live_Minikit_for_ESP1.TDO, MH-ET_Live_Minikit_for_ESP1.SD0

notes:
  Lüfter sollte an 12V für mehr Leistung

custom parts:
  MH-ET Live Minikit for ESP32: MH-ET Live Minikit for ESP32 ( http://mh.nodebb.com/topic/8/mh-et-live-minikit-for-esp32/2/) PCB footprint is invalid.
  BH1750: Light Sensor
  Adafruit BMP180: This precision sensor from Bosch is the best low-cost sensing solution for measuring barometric pressure and temperature. Because pressure changes with altitude you can also use it as an altimeter! The sensor is soldered onto a PCB with a 3.3V regulator, I2C level shifter and pull-up resistors on the I2C pins. The BMP180 is the next-generation of sensors from Bosch, and replaces the BMP085.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
  Small Fan, based on Fan - Ventilador: Small 2-pin fan, commonly used with single-board computers, 3d-printers, etc. This work is based on a much larger fan, as commonly found in desktop computers
