# Fritzing sketch ESP32_XIAO_2_13eink (saved by Fritzing 0.9.10b)
breadboards: 1

parts:
  Mod1 = seeeduino-xiao
  U2 = LIPO-110mAh [package=lipo-110]  # not connected
  A1 = Waveshare e-Paper HAT [package=THT]

nets:
  N1: Mod1.D0, A1.pin_3
  N2: Mod1.D1, A1.pin_2
  N3: Mod1.D3, A1.pin_4
  N4: Mod1.D8, A1.pin_5
  N5: Mod1.D10, A1.pin_6
  N6: Mod1.3V3, A1.pin_8
  N7: Mod1.GND, A1.pin_7

custom parts:
  seeeduino-xiao: Seeeduino XIAO processor board.
  Waveshare e-Paper HAT: .This is a universal driver board for e-Paper raw panels, can be used to drive various SPI interface e-Paper from Waveshare.
